# Fritzing sketch UltraSonic (saved by Fritzing 1.0.1rc)
breadboards: 1

parts:
  Part1 = Arduino Uno (Rev3)
  Part2 = HY-SRF05 Ultrasonic Rangefinder

nets:
  N1: Part1.D12/MISO, Part2.Echo
  N2: Part1.D13/SCK, Part2.Trig
  GND: Part1.GND, Part2.GND
  5V: Part1.5V, Part2.Vcc
